# Fritzing sketch JHHH-Smombie2go Schaltung (saved by Fritzing 0.9.3b)

parts:
  Bauteil1 = Arduino Nano (Rev3.0)
  V1 = DC Power [voltage=5]  # not connected
  S1 = Toggle Switch [package=THT]
  LED1 = LED - 5mm [color="Red (633nm)" package="5 mm [THT]"]
  JP1 = USB_MICROB_PLUG [package=micro-b-th]
  R1 = Resistor [tolerance=±5% resistance=330 package=THT]
  U1 = LIPO-2000mAh [package=lipo-2000]
  hc-sr1 = hc-sr04
  X1 = USB Connectors [package=usb-microb]

nets:
  GND: Bauteil1.GND, R1.Pin_0, U1.-, hc-sr1.GND
  N1: Bauteil1.D2, LED1.anode
  N2: Bauteil1.D3, hc-sr1.Echo
  VIN: Bauteil1.VIN, S1.COM, hc-sr1.VCC
  N3: S1.L1, U1.+, X1.D+
  GND_2: JP1.GND, X1.GND

notes:
  LiPo-Akku Laden
  Smartphone am
  LiPo-Akku Laden
  An/Aus
  Arduino
  Nano
  Warn-LED
  Ultraschallsensor
  LiPo-Akku
